# Fritzing sketch Wiring (saved by Fritzing 0.9.3b)
breadboards: 1

parts:
  U1 = ESP32S-HiLetgo [part_number=ESP32S-HiLetgo]
  Grove1 = Grove Dust Sensor
  U2 = MLX90614 [package=to-39]

nets:
  N1: U1.GND, U2.PWM_SDA
  N2: U1.GPIO10, U2.SCL_VZ
  VIN: U1.VIN, Grove1.GND, U2.VSS
  VCC: U1.GPIO6, Grove1.VCC, U2.VDD
  N3: U1.GPIO17, Grove1.SIG

custom parts:
  ESP32S-HiLetgo: HiLetgo ESP-WROOM-32 ESP32 ESP-32S Development Board 2.4GHz Dual-Mode WiFi + Bluetooth Dual Cores Microcontroller The ESP32 integrated with Antenna switches, RF Balun, power amplifiers, low-noise amplifiers, filters, and management modules, and the entire solution occupies the least area of PCB. 2.4 GHz Wi-Fi plus Bluetooth dual-mode chip, with TSMC Ultra-low power consumption 40nm technology,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
  Grove Dust Sensor: PPD42 Grove Dust Sensor
